# Fritzing sketch diagrama (saved by Fritzing 0.9.3b)
breadboards: 1

parts:
  SW1 = DIP Switch 8 Position [package=dipswitch-08]
  R1 = Resistor [tolerance=±5% resistance=220 package="0603 [SMD]"]
  R2 = Resistor [tolerance=±5% resistance=220 package="0603 [SMD]"]
  R3 = Resistor [tolerance=±5% resistance=220 package="0603 [SMD]"]
  R4 = Resistor [tolerance=±5% resistance=220 package="0603 [SMD]"]
  R5 = Resistor [tolerance=±5% resistance=220 package="0603 [SMD]"]
  LED1 = smd LED [color="Red (633nm)" package="0805 [SMD]"]
  LED2 = smd LED [color="Red (633nm)" package="0805 [SMD]"]
  R6 = Resistor [tolerance=±5% resistance=220 package="0603 [SMD]"]
  R7 = Resistor [tolerance=±5% resistance=220 package="0603 [SMD]"]
  R8 = Resistor [tolerance=±5% resistance=220 package="0603 [SMD]"]
  R9 = Resistor [tolerance=±5% resistance=220 package="0603 [SMD]"]
  R10 = Resistor [tolerance=±5% resistance=220 package="0603 [SMD]"]
  R11 = Resistor [tolerance=±5% resistance=220 package="0603 [SMD]"]
  SW2 = DIP Switch 8 Position [package=dipswitch-08]
  SW3 = DIP SWITCH [package=dipswitch-02]
  R12 = Resistor [tolerance=±5% resistance=220 package="0603 [SMD]"]
  R13 = Resistor [tolerance=±5% resistance=220 package="0603 [SMD]"]
  R14 = Resistor [tolerance=±5% resistance=220 package="0603 [SMD]"]
  LED3 = smd LED [color="Red (633nm)" package="0805 [SMD]"]
  LED4 = smd LED [color="Red (633nm)" package="0805 [SMD]"]
  LED5 = smd LED [color="Red (633nm)" package="0805 [SMD]"]
  LED6 = smd LED [color="Red (633nm)" package="0805 [SMD]"]
  LED7 = smd LED [color="Green (555nm)" package="0805 [SMD]"]
  LED8 = smd LED [color="Green (555nm)" package="0805 [SMD]"]
  LED9 = smd LED [color="Green (555nm)" package="0805 [SMD]"]
  LED10 = smd LED [color="Green (555nm)" package="0805 [SMD]"]
  Componente2 = Arduino Mega 2560 (Rev3)

nets:
  N1: SW1.1, SW1.2, SW1.3, SW1.4, SW1.8, LED1.cathode, LED2.cathode, SW2.1, SW2.2, SW2.3, SW2.4, SW2.5, SW2.6, SW2.7, SW2.8, SW3.2, LED3.cathode, LED4.cathode, LED5.cathode, LED6.cathode, Componente2.3V3
  N2: SW1.9, R5.Pin_0, Componente2.D45
  N3: SW1.13, R4.Pin_0, Componente2.D47
  N4: SW1.14, R3.Pin_0, Componente2.D49
  N5: SW1.15, R2.Pin_0, Componente2.D51
  N6: SW1.16, R1.Pin_0, Componente2.D53
  N7: R1.Pin_1, R2.Pin_1, R3.Pin_1, R4.Pin_1, R5.Pin_1, R6.Pin_1, R7.Pin_1, R8.Pin_1, R9.Pin_1, R10.Pin_1, R11.Pin_1, R12.Pin_1, R13.Pin_1, R14.Pin_1, LED7.cathode, LED8.cathode, LED9.cathode, LED10.cathode, Componente2.GND
  N8: LED1.anode, Componente2.D43
  N9: LED2.anode, Componente2.D23
  N10: R6.Pin_0, SW2.16, Componente2.D41
  N11: R7.Pin_0, SW2.15, Componente2.D39
  N12: R8.Pin_0, SW2.14, Componente2.D37
  N13: R9.Pin_0, SW2.13, Componente2.D35
  N14: R10.Pin_0, SW2.12, Componente2.D33
  N15: R11.Pin_0, SW3.3, Componente2.D25
  N16: SW2.9, R14.Pin_0, Componente2.D27
  N17: SW2.10, R13.Pin_0, Componente2.D29
  N18: SW2.11, R12.Pin_0, Componente2.D31
  N19: LED3.anode, Componente2.D44
  N20: LED4.anode, Componente2.D42
  N21: LED5.anode, Componente2.D40
  N22: LED6.anode, Componente2.D38
  N23: LED7.anode, Componente2.D52
  N24: LED8.anode, Componente2.D50
  N25: LED9.anode, Componente2.D48
  N26: LED10.anode, Componente2.D46
  N27: Componente2.D30, Componente2.D32
  N28: Componente2.D34, Componente2.D36
